# Fritzing sketch led_array (saved by Fritzing 0.8.5b)
breadboards: 2

parts:
  Part1 = LED Matrix - Serial Interface - Red/Green/Blue
  R1 = Resistor [tolerance=±5% resistance=1k package=THT]
  R2 = Resistor [tolerance=±5% resistance=1k package=THT]
  R3 = Resistor [tolerance=±5% resistance=1k package=THT]
  R4 = Resistor [tolerance=±5% resistance=1k package=THT]
  R5 = Resistor [tolerance=±5% resistance=1k package=THT]
  R6 = Resistor [tolerance=±5% resistance=1k package=THT]
  R7 = Resistor [tolerance=±5% resistance=1k package=THT]
  R8 = Resistor [tolerance=±5% resistance=1k package=THT]
  Part2 = Arduino Uno (Rev3)

nets:
  N1: Part1.VCC, R1.Pin_0, R7.Pin_1, Part2.D13/SCK, Part2.D2
  N2: Part1.SCK, Part2.D11_PWM/MOSI, Part2.D3_PWM
  N3: Part1.CS, R8.Pin_1, Part2.D7
  N4: Part1.MISO, Part2.A2
  N5: Part1.GND, R2.Pin_0, Part2.A3
  N6: Part1.MOSI, R3.Pin_0
  N7: R1.Pin_1, Part2.D6_PWM
  N8: R2.Pin_1, Part2.D9_PWM
  N9: R3.Pin_1, Part2.D8
  N10: R4.Pin_1, Part2.D5_PWM
  N11: R5.Pin_1, Part2.D4
  N12: R6.Pin_0, Part2.A0
  N13: R7.Pin_0, Part2.D12/MISO
  N14: R8.Pin_0, Part2.D10_PWM/SS
